// Logisim project gab12.circ as structural Verilog: 10 circuits, main circuit main
module main (
  input  in_1,
  input  in_2,
  input  in_3,
  input  in_4,
  input  in_5,
  input  in_6,
  input  carry_in,
  input  in_8,
  input  in_9,
  input  in_10,
  input  in_11,
  input  in_12,
  input  in_13,
  input  in_14,
  input  in_15,
  input  in_16,
  output soma,
  output soma_2,
  output carry,
  output soma_3,
  output carry_2,
  output soma_4,
  output carry_3,
  output out_24,
  output out_25,
  output soma_5,
  output out_27,
  output out_28,
  output out_29,
  output soma_6,
  output carry_4
);

  wire adder_3_cout, adder_5_cout, adder_7_cout, undriven_3;
  wire [3:1] adder_7_out, undriven, undriven_2;

  Adder #(.width(1)) adder_1 (.a(in_3), .b(in_4), .out(soma_2), .cout(carry));  // open: cin
  Adder #(.width(1)) adder_2 (.a(in_8), .b(in_9), .out(soma_4), .cin(carry_in), .cout(carry_3));
  Adder #(.width(1)) adder_3 (.a(in_13), .b(in_14), .out(soma_5), .cout(adder_3_cout));  // open: cin
  Adder #(.width(1)) adder_4 (.a(in_15), .b(in_16), .out(soma_6), .cin(adder_3_cout), .cout(carry_4));
  Adder #(.width(1)) adder_5 (.a(in_1), .b(in_2), .out(soma), .cout(adder_5_cout));  // open: cin
  Adder #(.width(1)) adder_6 (.a(in_5), .b(in_6), .out(soma_3), .cin(adder_5_cout), .cout(carry_2));
  Adder #(.width(4)) adder_7 (
    .a({undriven, in_11}), .b({undriven_2, in_12}), .out({adder_7_out, out_24}), .cin(undriven_3),
    .cout(adder_7_cout));
  // Pins of 1 and 4 bits meet at {undriven_2, in_12}
  // Pins of 1 and 4 bits meet at {adder_7_out, out_24}
  // Pins of 1 and 4 bits meet at {undriven, in_11}

  assign out_25 = out_24;
  assign out_28 = out_24;
  assign out_29 = out_24;
endmodule

module exerc1 (
  input  in_1,
  input  in_2,
  input  in_3,
  input  in_4,
  input  carry_in,
  input  in_6,
  input  in_7,
  input  carry_in_2,
  input  in_9,
  input  in_10,
  output Carry,
  output Soma,
  output Soma_2,
  output carry_2,
  output Carry_3,
  output soma_3,
  output carry_4,
  output Soma_4
);

  wire and_2_out, and_3_out, xor_2_out;

  and and_1 (Carry, in_4, in_3);
  xor xor_1 (Soma_2, in_3, in_4);
  and and_2 (and_2_out, in_10, in_9);
  xor xor_2 (xor_2_out, in_9, in_10);
  and and_3 (and_3_out, carry_in_2, xor_2_out);
  xor xor_3 (Soma_4, carry_in_2, xor_2_out);
  or or_1 (Carry_3, and_2_out, and_3_out);
  Adder #(.width(1)) adder_1 (.a(in_1), .b(in_2), .out(Soma), .cout(carry_2));  // open: cin
  Adder #(.width(1)) adder_2 (.a(in_6), .b(in_7), .out(soma_3), .cin(carry_in), .cout(carry_4));

  // Notes on the sheet:
  //   CIRCUITO MEIO SOMADOR
  //   CIRCUITO SOMADOR COMPLETO
endmodule

module exerc2 (
  input  A,
  input  B,
  input  A_2,
  input  B_2,
  input  A_3,
  input  B_3,
  input  A_4,
  input  B_4,
  output SOMA_bit_LSB,
  output out_10,
  output out_11,
  output SOMA__bit_MSB,
  output CARRY
);

  wire adder_1_cout, adder_2_cout, adder_3_cout;

  Adder #(.width(1)) adder_1 (.a(A), .b(B), .out(SOMA_bit_LSB), .cout(adder_1_cout));  // open: cin
  Adder #(.width(1)) adder_2 (.a(A_2), .b(B_2), .out(out_10), .cin(adder_1_cout), .cout(adder_2_cout));
  Adder #(.width(1)) adder_3 (.a(A_3), .b(B_3), .out(out_11), .cin(adder_2_cout), .cout(adder_3_cout));
  Adder #(.width(1)) adder_4 (.a(A_4), .b(B_4), .out(SOMA__bit_MSB), .cin(adder_3_cout), .cout(CARRY));
endmodule

module exerc3 (
  input  [3:0] A,
  input  [3:0] B,
  output out_3,
  output [3:0] out_4
);

  Adder #(.width(4)) adder_1 (.a(A), .b(B), .out(out_4), .cout(out_3));  // open: cin
endmodule

module exerc4 (
  input  [3:0] A,
  input  [3:0] A_2,
  input  [3:0] B,
  input  [3:0] B_2,
  output out_5,
  output [3:0] out_6,
  output [3:0] out_7
);

  wire adder_1_cout;

  Adder #(.width(4)) adder_1 (.a(A_2), .b(B_2), .out(out_7), .cout(adder_1_cout));  // open: cin
  Adder #(.width(4)) adder_2 (.a(A), .b(B), .out(out_6), .cin(adder_1_cout), .cout(out_5));
endmodule

module exerc5 (
  input  [3:0] in_1,
  input  [3:0] in_2,
  output out_3,
  output [3:0] out_4
);

  Subtractor #(.width(4)) subtractor_1 (.a(in_1), .b(in_2), .out(out_4), .bout(out_3));  // open: bin
endmodule

module exerc6 (
  input  [3:0] in_1,
  output [3:0] out_2
);

  Negator #(.width(4)) negator_1 (.in(in_1), .out(out_2));

  // Notes on the sheet:
  //   ex.:
  //   Complemento de 2
  //   [+] 0110
  //   1001
  //   +1
  //   [-] 1010
endmodule

module exerc7 (
  input  [3:0] in_1,
  input  [3:0] in_2,
  input  [3:0] in_3,
  input  [3:0] in_4,
  input  [3:0] in_5,
  input  [3:0] in_6,
  input  [3:0] in_7,
  output out_8,
  output [3:0] out_9,
  output out_10,
  output [3:0] out_11,
  output [3:0] out_12,
  output out_13,
  output [3:0] out_14
);

  wire [3:0] negator_1_out;

  Negator #(.width(4)) negator_1 (.in(in_2), .out(negator_1_out));
  Subtractor #(.width(4)) subtractor_1 (.a(in_3), .b(in_4), .out(out_12), .bout(out_10));  // open: bin
  Adder #(.width(4)) adder_1 (.a(in_1), .b(negator_1_out), .out(out_9), .cout(out_8));  // open: cin
  Adder #(.width(4)) adder_2 (.a(in_6), .b(in_7), .out(out_14), .cout(out_13));  // open: cin
  Negator #(.width(4)) negator_2 (.in(in_5), .out(out_11));
endmodule

module exerc8 (
  input  [3:0] in_1,
  input  [3:0] in_2,
  output [3:0] out_3,
  output [3:0] out_4
);

  Multiplier #(.width(4)) multiplier_1 (.a(in_1), .b(in_2), .out(out_4), .cout(out_3));  // open: cin

  // Notes on the sheet:
  //   Para uma multiplicação com 4 bits o número máximo de bits da resposta é 8. 
endmodule

module exerc9 (
  input  [3:0] in_1,
  input  [3:0] in_2,
  output out_3,
  output out_4,
  output out_5
);

  Comparator #(.width(4)) comparator_1 (.a(in_1), .b(in_2), .gt(out_3), .eq(out_4), .lt(out_5));
endmodule
