// Logisim project intcomp.Gabriela.circ as structural Verilog: 5 circuits, main circuit EXERX1
module EXERX1 (
  input  A,
  input  B,
  input  C,
  output S
);

  wire not_1_out, or_1_out, or_2_out;

  not not_1 (not_1_out, B);
  or or_1 (or_1_out, A, B);
  or or_2 (or_2_out, not_1_out, C);
  and and_1 (S, or_1_out, or_2_out);

  // Notes on the sheet:
  //   S = (A+B).(~B+C)
endmodule

module EX2 (
  input  A,
  input  B,
  input  C,
  output S
);

  wire and_1_out, and_2_out, nand_1_out, not_1_out;

  and and_1 (and_1_out, A, C);
  nand nand_1 (nand_1_out, B, C, C);
  not not_1 (not_1_out, A);
  and and_2 (and_2_out, C, B, not_1_out);
  or or_1 (S, and_1_out, nand_1_out, and_2_out);
endmodule

module EX3 (
  input  A,
  input  B,
  input  C,
  input  D,
  output S
);

  wire and_1_out, nand_1_out, not_1_out;

  not not_1 (not_1_out, C);
  and and_1 (and_1_out, A, B);
  nand nand_1 (nand_1_out, C, D);
  or or_1 (S, and_1_out, not_1_out, nand_1_out);
endmodule

module EX4 (
  input  X,
  input  Y,
  input  W,
  output Z
);

  wire not_1_out, or_1_out;

  not not_1 (not_1_out, Y);
  or or_1 (or_1_out, not_1_out, W);
  and and_1 (Z, X, or_1_out);
endmodule

module Ex5 (
  input  in_1,
  input  in_2,
  input  in_3,
  input  in_4,
  output out_5,
  output out_6
);

  wire and_1_out, and_2_out, not_1_out, not_2_out;

  not not_1 (not_1_out, in_1);
  not not_2 (not_2_out, in_2);
  and and_1 (and_1_out, not_1_out, in_2);
  and and_2 (and_2_out, in_1, not_2_out);
  xor xor_1 (out_6, in_3, in_4);
  or or_1 (out_5, and_1_out, and_2_out);
endmodule
